// Logisim project dalmia_abhay.circ as structural Verilog: 8 circuits, main circuit main
module main (
);

  wire ACTUALLYHALTED, and_3_out, and_4_out, and_5_out, and_6_out, and_7_out, bitselector_8_out,
       bitselector_9_out, CLK, comparator_1_eq, comparator_1_gt, comparator_1_lt, comparator_2_eq,
       comparator_3_eq, DBUF_BMUX, DBUF_MEMWR, DBUF_REGLD, DBUF_REGWR, EBUF_MEMWR, EBUF_REGLD, EBUF_REGWR,
       FBUF_BMUX, FBUF_MEMWR, FBUF_REGLD, FBUF_REGWR, FLUSH, forwarding_1_mux, forwarding_2_mux, HALT, MEMWR,
       MEMWRFinal, nor_1_out, not_1_out, or_1_out, or_5_out, or_6_out, or_7_out, or_8_out, or_9_out;
  wire [0:0] rom_1_data;
  wire [1:0] ALUFUNC, cond, DBUF_ALUFUNC, DBUF_cond, DBUF_MEMOUT, EBUF_MEMOUT, FBUF_MEMOUT, MBUF_MEMOUT,
       PCMUX;
  wire [2:0] DBUF_update, EBUF_update, MBUF_update, or_2_out, update;
  wire [3:0] DBUF_Rx, EBUF_Rx, IR_3_0, IR_23_20, IR_27_24, MBUF_Rx, opcode, SR2;
  wire [19:0] Imm;
  wire [23:0] bitselector_1_out, bitselector_7_out;
  wire [31:0] A, adder_1_out, AFinal, B, BFinal, bit_extender_1_out, bit_extender_2_out, BRPC, DBUF_A,
       DBUF_B, DBUF_Imm, DBUF_NPC, DBUF_RxVal, EBUF_A, EBUF_B, EBUF_NPC, EBUF_RAM, EBUF_Result, EBUF_RxVal,
       EBUF_RxValUpd, FBUF_NPC, forwarding_1_out, forwarding_2_out, if_idrr_buffer_1_fbuf_ir, IR, MBUF_NPC,
       MBUF_RAM, MBUF_Result, MBUF_RxVal, MBUF_RxValUpd, MEMDATA, multiplexer_1_out, multiplexer_5_out, PC_q,
       Result;

  Clock clock_1 (.out(CLK));
  not not_1 (not_1_out, or_1_out);
  or or_1 (or_1_out, FLUSH, ACTUALLYHALTED);
  Register #(.width(32)) PC (.D(multiplexer_1_out), .en(not_1_out), .Q(PC_q), .clk(CLK));  // open: clr
  S_R_Flip_Flop s_r_ff_1 (.S(HALT), .clk(CLK), .R(1'b0), .Q(ACTUALLYHALTED));  // open: Qn, preset, reset, en
  Adder #(.width(32)) adder_1 (.a(PC_q), .b(32'h1), .out(adder_1_out));  // open: cin, cout
  BitSelector #(.width(32), .group(24)) bitselector_1 (.in(PC_q), .out(bitselector_1_out), .sel(1'b0));
  Multiplexer #(.select(2), .width(32)) multiplexer_1 (
    .in0(adder_1_out), .in1(BRPC), .in2(BRPC), .in3(A), .out(multiplexer_1_out), .sel(PCMUX), .en(1'b1));
  RAM #(.addrWidth(24), .dataWidth(32)) ram_1 (
    .addr(bitselector_1_out), .data(IR), .clk(CLK), .ld(1'b1));  // open: sel, clr
  or or_2 (or_2_out[0], DBUF_update[0], DBUF_update[1], DBUF_update[2]);
  or or_3 (or_2_out[1], EBUF_update[0], EBUF_update[1], EBUF_update[2]);
  or or_4 (or_2_out[2], MBUF_update[0], MBUF_update[1], MBUF_update[2]);
  ROM #(.addrWidth(4), .dataWidth(14)) rom_1 (
    .addr(opcode),
    .data({update, cond, FBUF_BMUX, FBUF_MEMOUT, FBUF_REGWR, FBUF_REGLD, FBUF_MEMWR, ALUFUNC, rom_1_data[0]}));  // open: sel
  IF_IDRR_Buffer if_idrr_buffer_1 (
    .CLK(CLK), .IR(IR), .NPC(adder_1_out), .CLR(ACTUALLYHALTED), .DISABLE(FLUSH),
    .FBUF_IR(if_idrr_buffer_1_fbuf_ir), .FBUF_NPC(FBUF_NPC));
  or or_5 (or_5_out, MBUF_Rx[0], MBUF_Rx[1], MBUF_Rx[2], MBUF_Rx[3]);
  and and_1 (MEMWRFinal, MEMWR, or_5_out);
  BitSelector #(.width(32), .group(4)) bitselector_2 (.in(if_idrr_buffer_1_fbuf_ir), .out(IR_3_0), .sel(3'b000));
  BitSelector #(.width(32), .group(4)) bitselector_3 (.in(if_idrr_buffer_1_fbuf_ir), .out(IR_23_20), .sel(3'b101));
  BitSelector #(.width(32), .group(4)) bitselector_4 (.in(if_idrr_buffer_1_fbuf_ir), .out(IR_27_24), .sel(3'b110));
  BitSelector #(.width(32), .group(4)) bitselector_5 (.in(if_idrr_buffer_1_fbuf_ir), .out(opcode), .sel(3'b111));
  BitSelector #(.width(32), .group(20)) bitselector_6 (.in(if_idrr_buffer_1_fbuf_ir), .out(Imm), .sel(1'b0));
  and and_2 (HALT, opcode[0], opcode[1], opcode[2], opcode[3]);
  forwarding forwarding_1 (
    .SR(IR_23_20), .DBUF_Rx(DBUF_Rx), .EBUF_Rx(EBUF_Rx), .MBUF_Rx(MBUF_Rx), .DBUF_val(DBUF_RxVal),
    .EBUF_val(EBUF_RxValUpd), .MBUF_val(MBUF_RxValUpd), .update(or_2_out), .OUT(forwarding_1_out),
    .MUX(forwarding_1_mux));
  forwarding forwarding_2 (
    .SR(SR2), .DBUF_Rx(DBUF_Rx), .EBUF_Rx(EBUF_Rx), .MBUF_Rx(MBUF_Rx), .DBUF_val(DBUF_RxVal),
    .EBUF_val(EBUF_RxValUpd), .MBUF_val(MBUF_RxValUpd), .update(or_2_out), .OUT(forwarding_2_out),
    .MUX(forwarding_2_mux));
  Multiplexer #(.width(4)) multiplexer_2 (.in0(IR_3_0), .in1(IR_27_24), .out(SR2), .sel(rom_1_data[0]), .en(1'b1));
  assign bit_extender_1_out = {{12{Imm[19]}}, Imm};  // Bit_Extender bit_extender_1
  Adder #(.width(32)) adder_2 (.a(FBUF_NPC), .b(bit_extender_1_out), .out(BRPC));  // open: cin, cout
  Multiplexer #(.width(32)) multiplexer_3 (
    .in0(AFinal), .in1(forwarding_1_out), .out(A), .sel(forwarding_1_mux), .en(1'b1));
  Multiplexer #(.width(32)) multiplexer_4 (
    .in0(BFinal), .in1(forwarding_2_out), .out(B), .sel(forwarding_2_mux), .en(1'b1));
  Comparator #(.width(32)) comparator_1 (
    .a(A), .b(B), .gt(comparator_1_gt), .eq(comparator_1_eq), .lt(comparator_1_lt));
  or or_6 (or_6_out, comparator_1_gt, comparator_1_lt);
  and and_3 (and_3_out, ~cond[0], cond[1]);  // AND_Gate
  and and_4 (and_4_out, cond[0], ~cond[1]);  // AND_Gate
  and and_5 (and_5_out, cond[0], cond[1]);
  Dual_Ported_Register_File dual_ported_register_file_1 (
    .CLK(CLK), .WrEN(MEMWRFinal), .OUT1(AFinal), .WrREGNO(MBUF_Rx), .RdREGNO1(IR_23_20), .RdREGNO2(SR2),
    .OUT2(BFinal), .INPUT(MEMDATA));
  assign bit_extender_2_out = {{12{Imm[19]}}, Imm};  // Bit_Extender bit_extender_2
  and and_6 (and_6_out, or_6_out, and_3_out);
  and and_7 (and_7_out, comparator_1_eq, and_4_out);
  or or_7 (or_7_out, and_6_out, and_7_out);
  assign PCMUX = or_7_out ? 2'b10 : 2'bz;  // Controlled_Buffer controlled_buffer_1
  assign PCMUX = and_5_out ? 2'b11 : 2'bz;  // Controlled_Buffer controlled_buffer_2
  nor nor_1 (nor_1_out, or_7_out, and_5_out);
  assign PCMUX = nor_1_out ? 2'b00 : 2'bz;  // Controlled_Buffer controlled_buffer_3
  or or_8 (or_8_out, FLUSH, ACTUALLYHALTED);
  IDRR_EX_Buffer idrr_ex_buffer_1 (
    .CLK(CLK), .A(A), .B(B), .FBUF_NPC(FBUF_NPC), .Imm(bit_extender_2_out), .FBUF_MEMWR(FBUF_MEMWR),
    .FBUF_REGLD(FBUF_REGLD), .FBUF_REGWR(FBUF_REGWR), .FBUF_MEMOUT(FBUF_MEMOUT), .FBUF_BMUX(FBUF_BMUX),
    .FBUF_Rx(IR_27_24), .FBUF_update(update), .FBUF_cond(cond), .FBUF_ALUFUNC(ALUFUNC), .CLEAR(or_8_out),
    .DBUF_A(DBUF_A), .DBUF_B(DBUF_B), .DBUF_NPC(DBUF_NPC), .DBUF_Imm(DBUF_Imm), .DBUF_MEMWR(DBUF_MEMWR),
    .DBUF_REGLD(DBUF_REGLD), .DBUF_REGWR(DBUF_REGWR), .DBUF_MEMOUT(DBUF_MEMOUT), .DBUF_BMUX(DBUF_BMUX),
    .DBUF_Rx(DBUF_Rx), .DBUF_update(DBUF_update), .DBUF_cond(DBUF_cond), .DBUF_ALUFUNC(DBUF_ALUFUNC));
  Comparator #(.width(4)) comparator_2 (.a(DBUF_Rx), .b(IR_23_20), .eq(comparator_2_eq));  // open: gt, lt
  Comparator #(.width(4)) comparator_3 (.a(DBUF_Rx), .b(SR2), .eq(comparator_3_eq));  // open: gt, lt
  or or_9 (or_9_out, comparator_2_eq, comparator_3_eq);
  and and_8 (FLUSH, DBUF_REGLD, or_9_out);
  Multiplexer #(.width(32)) multiplexer_5 (
    .in0(DBUF_B), .in1(DBUF_Imm), .out(multiplexer_5_out), .sel(DBUF_BMUX), .en(1'b1));
  ALU alu_1 (.A(DBUF_A), .B(multiplexer_5_out), .NPC(DBUF_NPC), .SB(DBUF_ALUFUNC), .out_5(Result));
  Multiplexer #(.select(2), .width(32)) multiplexer_6 (
    .in0(Result), .in1(Result), .in2(Result), .in3(DBUF_NPC), .out(DBUF_RxVal), .sel(DBUF_cond));  // open: en
  EX_MEM_Buffer ex_mem_buffer_1 (
    .CLK(CLK), .Result(Result), .DBUF_NPC(DBUF_NPC), .DBUF_A(DBUF_A), .DBUF_MEMWR(DBUF_MEMWR),
    .DBUF_REGLD(DBUF_REGLD), .DBUF_REGWR(DBUF_REGWR), .DBUF_MEMOUT(DBUF_MEMOUT), .DBUF_Rx(DBUF_Rx),
    .DBUF_update(DBUF_update), .DBUF_RxValue(DBUF_RxVal), .DBUF_B(DBUF_B), .EBUF_Result(EBUF_Result),
    .EBUF_NPC(EBUF_NPC), .EBUF_A(EBUF_A), .EBUF_MEMWR(EBUF_MEMWR), .EBUF_REGLD(EBUF_REGLD),
    .EBUF_REGWR(EBUF_REGWR), .EBUF_MEMOUT(EBUF_MEMOUT), .EBUF_Rx(EBUF_Rx), .EBUF_update(EBUF_update),
    .EBUF_RxValue(EBUF_RxVal), .EBUF_B(EBUF_B));
  BitSelector #(.width(32), .group(24)) bitselector_7 (.in(EBUF_Result), .out(bitselector_7_out), .sel(1'b0));
  RAM #(.addrWidth(24), .dataWidth(32), .bus("separate")) ram_2 (
    .addr(bitselector_7_out), .din(EBUF_B), .data(EBUF_RAM), .str(EBUF_REGWR), .clk(CLK), .ld(EBUF_REGLD));  // open: sel, clr
  Multiplexer #(.width(32)) multiplexer_7 (
    .in0(EBUF_RxVal), .in1(EBUF_RAM), .out(EBUF_RxValUpd), .sel(bitselector_8_out), .en(1'b1));
  BitSelector #(.width(3)) bitselector_8 (.in(EBUF_update), .out(bitselector_8_out), .sel(2'b01));
  BitSelector #(.width(3)) bitselector_9 (.in(MBUF_update), .out(bitselector_9_out), .sel(2'b00));
  MEM_WB_Buffer mem_wb_buffer_1 (
    .CLK(CLK), .EBUF_MEMWR(EBUF_MEMWR), .EBUF_MEMOUT(EBUF_MEMOUT), .EBUF_NPC(EBUF_NPC),
    .EBUF_Result(EBUF_Result), .EBUF_RAM(EBUF_RAM), .EBUF_Rx(EBUF_Rx), .EBUF_update(EBUF_update),
    .EBUF_RxVal(EBUF_RxValUpd), .MBUF_MEMWR(MEMWR), .MBUF_MEMOUT(MBUF_MEMOUT), .MBUF_NPC(MBUF_NPC),
    .MBUF_A(MBUF_Result), .MBUF_RAM(MBUF_RAM), .MBUF_Rx(MBUF_Rx), .MBUF_update(MBUF_update),
    .MBUF_RxVal(MBUF_RxVal));
  Multiplexer #(.select(2), .width(32)) multiplexer_8 (
    .in0(MBUF_RAM), .in1(MBUF_Result), .in2(MBUF_NPC), .out(MEMDATA), .sel(MBUF_MEMOUT), .en(1'b1));  // open: in3
  Multiplexer #(.width(32)) multiplexer_9 (
    .in0(MBUF_RxVal), .in1(MEMDATA), .out(MBUF_RxValUpd), .sel(bitselector_9_out), .en(1'b1));

  // Other names for the same wires on the sheet: JALRPC[31:0] = A; SR1[3:0] = IR_23_20

  // Notes on the sheet:
  //   contents of rom_1 (hex, n*v repeats v):
  //   2848 2948 284a 241 2e88 1918 294c 161 294e 441
endmodule

module Dual_Ported_Register_File (
  input  CLK,
  input  WrEN,
  input  [3:0] WrREGNO,
  input  [3:0] RdREGNO1,
  input  [3:0] RdREGNO2,
  input  [31:0] INPUT,
  output [31:0] OUT1,
  output [31:0] OUT2
);

  wire En_a0, En_a1, En_a2, En_at, En_fp, En_k0, En_ra, En_s0, En_s1, En_s2, En_sp, En_t0, En_t1, En_t2,
       En_v0;
  wire [31:0] a0, a1, a2, at, fp, k0, ra, s0, s1, s2, sp, t0, t1, t2, v0, zero;

  Decoder #(.select(4), .disabled(0)) decoder_1 (
    .out1(En_at), .out2(En_v0), .out3(En_a0), .out4(En_a1), .out5(En_a2), .out6(En_t0), .out7(En_t1),
    .out8(En_t2), .out9(En_s0), .out10(En_s1), .out11(En_s2), .out12(En_k0), .out13(En_sp), .out14(En_fp),
    .out15(En_ra), .sel(WrREGNO), .en(WrEN));  // open: out0
  Register #(.width(32)) u_zero (.D(INPUT), .en(1'b0), .Q(zero), .clk(CLK));  // open: clr
  Register #(.width(32)) u_at (.D(INPUT), .en(En_at), .Q(at), .clk(CLK));  // open: clr
  Register #(.width(32)) u_v0 (.D(INPUT), .en(En_v0), .Q(v0), .clk(CLK));  // open: clr
  Register #(.width(32)) u_a0 (.D(INPUT), .en(En_a0), .Q(a0), .clk(CLK));  // open: clr
  Register #(.width(32)) u_a1 (.D(INPUT), .en(En_a1), .Q(a1), .clk(CLK));  // open: clr
  Register #(.width(32)) u_a2 (.D(INPUT), .en(En_a2), .Q(a2), .clk(CLK));  // open: clr
  Register #(.width(32)) u_t0 (.D(INPUT), .en(En_t0), .Q(t0), .clk(CLK));  // open: clr
  Register #(.width(32)) u_t1 (.D(INPUT), .en(En_t1), .Q(t1), .clk(CLK));  // open: clr
  Multiplexer #(.select(4), .width(32), .disabled(0), .enable("false")) multiplexer_1 (
    .in0(zero), .in1(at), .in2(v0), .in3(a0), .in4(a1), .in5(a2), .in6(t0), .in7(t1), .in8(t2), .in9(s0),
    .in10(s1), .in11(s2), .in12(k0), .in13(sp), .in14(fp), .in15(ra), .out(OUT2), .sel(RdREGNO2));
  Register #(.width(32)) u_t2 (.D(INPUT), .en(En_t2), .Q(t2), .clk(CLK));  // open: clr
  Register #(.width(32)) u_s0 (.D(INPUT), .en(En_s0), .Q(s0), .clk(CLK));  // open: clr
  Register #(.width(32)) u_s1 (.D(INPUT), .en(En_s1), .Q(s1), .clk(CLK));  // open: clr
  Register #(.width(32)) u_s2 (.D(INPUT), .en(En_s2), .Q(s2), .clk(CLK));  // open: clr
  Register #(.width(32)) u_k0 (.D(INPUT), .en(En_k0), .Q(k0), .clk(CLK));  // open: clr
  Register #(.width(32)) u_sp (.D(INPUT), .en(En_sp), .Q(sp), .clk(CLK));  // open: clr
  Register #(.width(32)) u_fp (.D(INPUT), .en(En_fp), .Q(fp), .clk(CLK));  // open: clr
  Register #(.width(32)) u_ra (.D(INPUT), .en(En_ra), .Q(ra), .clk(CLK));  // open: clr
  Multiplexer #(.select(4), .width(32), .disabled(0), .enable("false")) multiplexer_2 (
    .in0(zero), .in1(at), .in2(v0), .in3(a0), .in4(a1), .in5(a2), .in6(t0), .in7(t1), .in8(t2), .in9(s0),
    .in10(s1), .in11(s2), .in12(k0), .in13(sp), .in14(fp), .in15(ra), .out(OUT1), .sel(RdREGNO1));

  // Notes on the sheet:
  //   MODIFY AT YOUR OWN RISK
endmodule

module IF_IDRR_Buffer (
  input  CLK,
  input  [31:0] IR,
  input  [31:0] NPC,
  input  CLR,
  input  DISABLE,
  output [31:0] FBUF_IR,
  output [31:0] FBUF_NPC
);

  wire DISABLE_t;
  wire [31:0] multiplexer_1_out, multiplexer_2_out;

  Multiplexer #(.width(32)) multiplexer_1 (.in0(IR), .in1({32{1'b0}}), .out(multiplexer_1_out), .sel(CLR));  // open: en
  Multiplexer #(.width(32)) multiplexer_2 (
    .in0(NPC), .in1({32{1'b0}}), .out(multiplexer_2_out), .sel(CLR));  // open: en
  Register #(.width(32)) register_1 (.D(multiplexer_1_out), .en(DISABLE_t), .Q(FBUF_IR), .clk(CLK));  // open: clr
  Register #(.width(32)) register_2 (.D(multiplexer_2_out), .en(DISABLE_t), .Q(FBUF_NPC), .clk(CLK));  // open: clr
  not not_1 (DISABLE_t, DISABLE);
endmodule

module IDRR_EX_Buffer (
  input  CLK,
  input  [31:0] A,
  input  [31:0] B,
  input  [31:0] FBUF_NPC,
  input  [31:0] Imm,
  input  FBUF_MEMWR,
  input  FBUF_REGLD,
  input  FBUF_REGWR,
  input  [1:0] FBUF_MEMOUT,
  input  FBUF_BMUX,
  input  [3:0] FBUF_Rx,
  input  [2:0] FBUF_update,
  input  [1:0] FBUF_cond,
  input  [1:0] FBUF_ALUFUNC,
  input  CLEAR,
  output [31:0] DBUF_A,
  output [31:0] DBUF_B,
  output [31:0] DBUF_NPC,
  output [31:0] DBUF_Imm,
  output DBUF_MEMWR,
  output DBUF_REGLD,
  output DBUF_REGWR,
  output [1:0] DBUF_MEMOUT,
  output DBUF_BMUX,
  output [3:0] DBUF_Rx,
  output [2:0] DBUF_update,
  output [1:0] DBUF_cond,
  output [1:0] DBUF_ALUFUNC
);

  wire multiplexer_5_out, multiplexer_6_out, multiplexer_7_out, multiplexer_9_out;
  wire [1:0] multiplexer_8_out, multiplexer_12_out, multiplexer_13_out;
  wire [2:0] multiplexer_11_out;
  wire [3:0] multiplexer_10_out;
  wire [31:0] multiplexer_1_out, multiplexer_2_out, multiplexer_3_out, multiplexer_4_out;

  Multiplexer #(.width(32)) multiplexer_1 (
    .in0(A), .in1({32{1'b0}}), .out(multiplexer_1_out), .sel(CLEAR));  // open: en
  Multiplexer #(.width(32)) multiplexer_2 (
    .in0(B), .in1({32{1'b0}}), .out(multiplexer_2_out), .sel(CLEAR));  // open: en
  Multiplexer #(.width(32)) multiplexer_3 (
    .in0(FBUF_NPC), .in1({32{1'b0}}), .out(multiplexer_3_out), .sel(CLEAR));  // open: en
  Multiplexer #(.width(32)) multiplexer_4 (
    .in0(Imm), .in1({32{1'b0}}), .out(multiplexer_4_out), .sel(CLEAR));  // open: en
  Multiplexer multiplexer_5 (.in0(FBUF_MEMWR), .in1(1'b1), .out(multiplexer_5_out), .sel(CLEAR));  // open: en
  Multiplexer multiplexer_6 (.in0(FBUF_REGLD), .in1(1'b0), .out(multiplexer_6_out), .sel(CLEAR));  // open: en
  Multiplexer multiplexer_7 (.in0(FBUF_REGWR), .in1(1'b0), .out(multiplexer_7_out), .sel(CLEAR));  // open: en
  Multiplexer #(.width(2)) multiplexer_8 (
    .in0(FBUF_MEMOUT), .in1(2'b01), .out(multiplexer_8_out), .sel(CLEAR));  // open: en
  Multiplexer multiplexer_9 (.in0(FBUF_BMUX), .in1(1'b0), .out(multiplexer_9_out), .sel(CLEAR));  // open: en
  Multiplexer #(.width(4)) multiplexer_10 (
    .in0(FBUF_Rx), .in1(4'b0000), .out(multiplexer_10_out), .sel(CLEAR));  // open: en
  Multiplexer #(.width(3)) multiplexer_11 (
    .in0(FBUF_update), .in1(3'b101), .out(multiplexer_11_out), .sel(CLEAR));  // open: en
  Multiplexer #(.width(2)) multiplexer_12 (
    .in0(FBUF_cond), .in1(2'b00), .out(multiplexer_12_out), .sel(CLEAR));  // open: en
  Multiplexer #(.width(2)) multiplexer_13 (
    .in0(FBUF_ALUFUNC), .in1(2'b00), .out(multiplexer_13_out), .sel(CLEAR));  // open: en
  Register #(.width(32)) register_1 (.D(multiplexer_1_out), .Q(DBUF_A), .clk(CLK));  // open: en, clr
  Register #(.width(32)) register_2 (.D(multiplexer_2_out), .Q(DBUF_B), .clk(CLK));  // open: en, clr
  Register #(.width(32)) register_3 (.D(multiplexer_3_out), .Q(DBUF_NPC), .clk(CLK));  // open: en, clr
  Register #(.width(32)) register_4 (.D(multiplexer_4_out), .Q(DBUF_Imm), .clk(CLK));  // open: en, clr
  Register #(.width(1)) register_5 (.D(multiplexer_5_out), .Q(DBUF_MEMWR), .clk(CLK));  // open: en, clr
  Register #(.width(1)) register_6 (.D(multiplexer_6_out), .Q(DBUF_REGLD), .clk(CLK));  // open: en, clr
  Register #(.width(1)) register_7 (.D(multiplexer_7_out), .Q(DBUF_REGWR), .clk(CLK));  // open: en, clr
  Register #(.width(2)) register_8 (.D(multiplexer_8_out), .Q(DBUF_MEMOUT), .clk(CLK));  // open: en, clr
  Register #(.width(1)) register_9 (.D(multiplexer_9_out), .Q(DBUF_BMUX), .clk(CLK));  // open: en, clr
  Register #(.width(4)) register_10 (.D(multiplexer_10_out), .Q(DBUF_Rx), .clk(CLK));  // open: en, clr
  Register #(.width(3)) register_11 (.D(multiplexer_11_out), .Q(DBUF_update), .clk(CLK));  // open: en, clr
  Register #(.width(2)) register_12 (.D(multiplexer_12_out), .Q(DBUF_cond), .clk(CLK));  // open: en, clr
  Register #(.width(2)) register_13 (.D(multiplexer_13_out), .Q(DBUF_ALUFUNC), .clk(CLK));  // open: en, clr

  // Other names for the same wires on the sheet: CLR = CLEAR
endmodule

module EX_MEM_Buffer (
  input  CLK,
  input  [31:0] Result,
  input  [31:0] DBUF_NPC,
  input  [31:0] DBUF_A,
  input  DBUF_MEMWR,
  input  DBUF_REGLD,
  input  DBUF_REGWR,
  input  [1:0] DBUF_MEMOUT,
  input  [3:0] DBUF_Rx,
  input  [2:0] DBUF_update,
  input  [31:0] DBUF_RxValue,
  input  [31:0] DBUF_B,
  output [31:0] EBUF_Result,
  output [31:0] EBUF_NPC,
  output [31:0] EBUF_A,
  output EBUF_MEMWR,
  output EBUF_REGLD,
  output EBUF_REGWR,
  output [1:0] EBUF_MEMOUT,
  output [3:0] EBUF_Rx,
  output [2:0] EBUF_update,
  output [31:0] EBUF_RxValue,
  output [31:0] EBUF_B
);

  Register #(.width(32)) register_1 (.D(Result), .Q(EBUF_Result), .clk(CLK));  // open: en, clr
  Register #(.width(32)) register_2 (.D(DBUF_NPC), .Q(EBUF_NPC), .clk(CLK));  // open: en, clr
  Register #(.width(32)) register_3 (.D(DBUF_A), .Q(EBUF_A), .clk(CLK));  // open: en, clr
  Register #(.width(1)) register_4 (.D(DBUF_MEMWR), .Q(EBUF_MEMWR), .clk(CLK));  // open: en, clr
  Register #(.width(1)) register_5 (.D(DBUF_REGLD), .Q(EBUF_REGLD), .clk(CLK));  // open: en, clr
  Register #(.width(1)) register_6 (.D(DBUF_REGWR), .Q(EBUF_REGWR), .clk(CLK));  // open: en, clr
  Register #(.width(2)) register_7 (.D(DBUF_MEMOUT), .Q(EBUF_MEMOUT), .clk(CLK));  // open: en, clr
  Register #(.width(4)) register_8 (.D(DBUF_Rx), .Q(EBUF_Rx), .clk(CLK));  // open: en, clr
  Register #(.width(3)) register_9 (.D(DBUF_update), .Q(EBUF_update), .clk(CLK));  // open: en, clr
  Register #(.width(32)) register_10 (.D(DBUF_RxValue), .Q(EBUF_RxValue), .clk(CLK));  // open: en, clr
  Register #(.width(32)) register_11 (.D(DBUF_B), .Q(EBUF_B), .clk(CLK));  // open: en, clr
endmodule

module MEM_WB_Buffer (
  input  CLK,
  input  EBUF_MEMWR,
  input  [1:0] EBUF_MEMOUT,
  input  [31:0] EBUF_NPC,
  input  [31:0] EBUF_Result,
  input  [31:0] EBUF_RAM,
  input  [3:0] EBUF_Rx,
  input  [2:0] EBUF_update,
  input  [31:0] EBUF_RxVal,
  output MBUF_MEMWR,
  output [1:0] MBUF_MEMOUT,
  output [31:0] MBUF_NPC,
  output [31:0] MBUF_A,
  output [31:0] MBUF_RAM,
  output [3:0] MBUF_Rx,
  output [2:0] MBUF_update,
  output [31:0] MBUF_RxVal
);

  Register #(.width(1)) register_1 (.D(EBUF_MEMWR), .Q(MBUF_MEMWR), .clk(CLK));  // open: en, clr
  Register #(.width(2)) register_2 (.D(EBUF_MEMOUT), .Q(MBUF_MEMOUT), .clk(CLK));  // open: en, clr
  Register #(.width(32)) register_3 (.D(EBUF_NPC), .Q(MBUF_NPC), .clk(CLK));  // open: en, clr
  Register #(.width(32)) register_4 (.D(EBUF_Result), .Q(MBUF_A), .clk(CLK));  // open: en, clr
  Register #(.width(32)) register_5 (.D(EBUF_RAM), .Q(MBUF_RAM), .clk(CLK));  // open: en, clr
  Register #(.width(4)) register_6 (.D(EBUF_Rx), .Q(MBUF_Rx), .clk(CLK));  // open: en, clr
  Register #(.width(3)) register_7 (.D(EBUF_update), .Q(MBUF_update), .clk(CLK));  // open: en, clr
  Register #(.width(32)) register_8 (.D(EBUF_RxVal), .Q(MBUF_RxVal), .clk(CLK));  // open: en, clr
endmodule

module ALU (
  input  [31:0] A,
  input  [31:0] B,
  input  [31:0] NPC,
  input  [1:0] SB,
  output [31:0] out_5
);

  wire [1:0] SBSFT;
  wire [4:0] bitselector_3_out;
  wire [31:0] adder_1_out, adder_2_out, nand_1_out, SHIFT, shifter_1_out, shifter_2_out, shifter_3_out;

  BitSelector #(.width(32)) bitselector_1 (.in(B), .out(SBSFT[0]), .sel(5'b10010));
  BitSelector #(.width(32)) bitselector_2 (.in(B), .out(SBSFT[1]), .sel(5'b10011));
  Adder #(.width(32)) adder_1 (.a(A), .b(B), .out(adder_1_out));  // open: cin, cout
  assign nand_1_out = ~(A & B);  // NAND_Gate nand_1, 32 bits wide
  Adder #(.width(32)) adder_2 (.a(B), .b(NPC), .out(adder_2_out));  // open: cin, cout
  BitSelector #(.width(32), .group(5)) bitselector_3 (.in(B), .out(bitselector_3_out), .sel(3'b000));
  Multiplexer #(.select(2), .width(32), .disabled(0), .enable("false")) multiplexer_1 (
    .in0(adder_1_out), .in1(nand_1_out), .in2(adder_2_out), .in3(SHIFT), .out(out_5), .sel(SB));
  Shifter #(.width(32)) shifter_1 (.in(A), .\dist (bitselector_3_out), .out(shifter_1_out));
  Shifter #(.width(32), .shift("lr")) shifter_2 (.in(A), .\dist (bitselector_3_out), .out(shifter_2_out));
  Shifter #(.width(32), .shift("ar")) shifter_3 (.in(A), .\dist (bitselector_3_out), .out(shifter_3_out));
  Multiplexer #(.select(2), .width(32), .disabled(0), .enable("false")) multiplexer_2 (
    .in0(shifter_1_out), .in1(shifter_2_out), .in2(shifter_1_out), .in3(shifter_3_out), .out(SHIFT),
    .sel(SBSFT));

  // Other names for the same wires on the sheet: ALUFunc[1:0] = SB
endmodule

module forwarding (
  input  [3:0] SR,
  input  [3:0] DBUF_Rx,
  input  [3:0] EBUF_Rx,
  input  [3:0] MBUF_Rx,
  input  [31:0] DBUF_val,
  input  [31:0] EBUF_val,
  input  [31:0] MBUF_val,
  input  [2:0] update,
  output [31:0] OUT,
  output MUX
);

  wire and_2_out, and_3_out, and_4_out, comparator_1_eq, comparator_2_eq, comparator_3_eq, cond1, cond2,
       cond3;

  Comparator #(.width(4)) comparator_1 (.a(SR), .b(DBUF_Rx), .eq(comparator_1_eq));  // open: gt, lt
  Comparator #(.width(4)) comparator_2 (.a(SR), .b(EBUF_Rx), .eq(comparator_2_eq));  // open: gt, lt
  Comparator #(.width(4)) comparator_3 (.a(SR), .b(MBUF_Rx), .eq(comparator_3_eq));  // open: gt, lt
  and and_1 (cond1, comparator_1_eq, update[0]);
  assign OUT = cond1 ? DBUF_val : 32'bz;  // Controlled_Buffer controlled_buffer_1
  and and_2 (and_2_out, ~cond1, comparator_2_eq);  // AND_Gate
  and and_3 (and_3_out, ~cond2, ~cond1, comparator_3_eq);  // AND_Gate
  and and_4 (and_4_out, ~cond1, ~cond2, ~cond3);  // AND_Gate
  and and_5 (cond2, and_2_out, update[1]);
  and and_6 (cond3, and_3_out, update[2]);
  assign OUT = and_4_out ? {32{1'b0}} : 32'bz;  // Controlled_Buffer controlled_buffer_2
  assign OUT = cond2 ? EBUF_val : 32'bz;  // Controlled_Buffer controlled_buffer_3
  assign OUT = cond3 ? MBUF_val : 32'bz;  // Controlled_Buffer controlled_buffer_4
  or or_1 (MUX, cond1, cond2, cond3);

  // Other names for the same wires on the sheet: DBUF[3:0] = DBUF_Rx; EBUF[3:0] = EBUF_Rx; MBUF[3:0] = MBUF_Rx;
  //   update1 = update[0]; update2 = update[1]; update3 = update[2]
endmodule
